# Fritzing sketch ControladorTemperatura (saved by Fritzing 0.7.10b)
breadboards: 1

parts:
  Arduino1 = Arduino
  Parte1 = Real Time Clock Module - DS1307 RTC Breakout Board
  LCD1 = LCD screen  # not connected
  U1 = 74HC595 [package="DIP16 [THT]"]  # not connected
  LED1 = Blue LED - 5mm [package="5 mm [THT]"]  # not connected
  LED3 = yellow LED - 5mm [package="5 mm [THT]"]  # not connected
  LED4 = LED - 5mm [color="Red (633nm)" package="5 mm [THT]"]  # not connected
  J1 = Piezo Speaker  # not connected
  R1 = Rotary Potentiometer (Large) [maximum_resistance=10kΩ package=THT]  # not connected
  T2 = TMP36 Temperature Sensor [package="TO92 [THT]"]  # not connected

nets:
  N1: Arduino1.D2, Parte1.SQW
  N2: Arduino1.A4, Parte1.SDA
  N3: Arduino1.A5, Parte1.SCL
